# Fritzing sketch final_project (saved by Fritzing 0.9.10b)
breadboards: 1

parts:
  J1 = STM32 Nucleo boards
  Part1 = Adafruit Ultimate GPS v3 [part_number="Adafruit #746"]
  Part2 = Adafruit Si7021 Humidity and Temperature Sensor [part_number="Adafruit #3251"]
  Q1 = LTR-301 [package=ltr-301]
  R1 = Resistor [tolerance=±5% resistance=220 package="0402 [SMD]"]

nets:
  N1: J1.A0, Q1.E, R1.Pin_0
  N2: J1.D0/RX, Part1.TX
  N3: J1.D1/TX, Part1.RX
  3V3: J1.3V3, Part2.VCC, Q1.C
  GND: J1.GND, Part1.VIN, Part1.GND, Part2.GND, R1.Pin_1

custom parts:
  Adafruit Ultimate GPS v3: We carry a few different GPS modules here in the Adafruit shop, but none that satisfied our every desire - that's why we designed this little GPS breakout board. We believe this is the Ultimate GPS module, so we named it that. It's got everything you want and more: -165 dBm sensitivity, 10 Hz updates, 66 channels 5V friendly design and only 20mA current draw Breadboard friendly + two mounting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
  Adafruit Si7021 Humidity and Temperature Sensor: It's summer and you're sweating and your hair's all frizzy and all you really want to know is why the weatherman said this morning that today's relative humidity would max out at a perfectly reasonable 42% when it feels more like 77%. Enter the Si7021 Temperature + Humidity Sensor - the best way to prove the weatherman wrong! This lovely sensor for Silicon labs has ± 3% relative humidity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
